# Fritzing sketch sketch (saved by Fritzing 0.9.6b)
breadboards: 1

parts:
  Part1 = Arduino Uno (Rev3)  # not connected
  WeMos_D1_Mini1 = WeMos D1 Mini
  WeMos_D1_Mini_OLED_Shield1 = WeMos D1 Mini OLED Shield
  R1 = Resistor [tolerance=±5% power=0.25 resistance=1k package=THT]
  R2 = Resistor [tolerance=±5% power=0.25 resistance=2.2k package=THT]
  Arduino_CNC_Shield_V3_00_1 = Arduino_CNC_V3.00
  M2 = Stepper Motor - Bipolar
  M3 = Stepper Motor - Bipolar
  J1 = Basic Servo
  Mod1 = YL-99 Limit switch and LED

nets:
  3V3: WeMos_D1_Mini1.3V3, WeMos_D1_Mini_OLED_Shield1.3V3
  5V: WeMos_D1_Mini1.5V, WeMos_D1_Mini_OLED_Shield1.5V, Arduino_CNC_Shield_V3_00_1.5V, J1.vcc
  N1: WeMos_D1_Mini1.D1, WeMos_D1_Mini_OLED_Shield1.D1
  N2: WeMos_D1_Mini1.D2, WeMos_D1_Mini_OLED_Shield1.D2
  N3: WeMos_D1_Mini1.D3, Arduino_CNC_Shield_V3_00_1.RX
  N4: WeMos_D1_Mini1.D4, R1.Pin_1, R2.Pin_0
  GND: WeMos_D1_Mini1.G, WeMos_D1_Mini_OLED_Shield1.G, R2.Pin_1, Arduino_CNC_Shield_V3_00_1.GND, J1.gnd
  N5: R1.Pin_0, Arduino_CNC_Shield_V3_00_1.TX
  N6: Arduino_CNC_Shield_V3_00_1.X-MTR_'1', M3.A
  N7: Arduino_CNC_Shield_V3_00_1.X-MTR_'2', M3.B
  N8: Arduino_CNC_Shield_V3_00_1.X-MTR_'3', M3.D
  N9: Arduino_CNC_Shield_V3_00_1.X-MTR_'4', M3.C
  N10: Arduino_CNC_Shield_V3_00_1.Z-MTR_'1', M2.A
  N11: Arduino_CNC_Shield_V3_00_1.Z-MTR_'2', M2.B
  N12: Arduino_CNC_Shield_V3_00_1.Z-MTR_'3', M2.D
  N13: Arduino_CNC_Shield_V3_00_1.Z-MTR_'4', M2.C
  N14: Arduino_CNC_Shield_V3_00_1.End_Stops_Z+_(Gnd), Mod1.GND
  N15: Arduino_CNC_Shield_V3_00_1.End_Stops_Z-_(and_Z+)_/_SpnEn, Mod1.VCC
  N16: Arduino_CNC_Shield_V3_00_1.SpnEn_/_Z_Limit, J1.pulse

notes:
  RS232
  - Arduino UNO + GRBL firmware
  - CNC Shield
  level shift 5V -> 3.3V:
  TX Arduino -> RX Wemos
  - user interface via http://
  - feeds G-code to CNC controller
  - line by line from file
  - from http api requests
  - spindle PWM as servo sigal
  - slightly modified GRBL firmware
  Z-limit switch

custom parts:
  Arduino_CNC_V3.00: Protoneer Arduino CNC Shield V3.00 If using Grbl V0.9: The “A” axis can not be used (yet). The “SCL” (Arduino A5) pin is now used for 'Probing' input. The “End Stops Z+ & Z-” (Arduino D11) and “SpnEn” (Arduino D12) have been switched!
